# Fritzing sketch Train (saved by Fritzing 0.9.3b)
breadboards: 1
perfboards: 1

parts:
  R1 = Resistor [tolerance=±5% resistance=3.3k package="2010 [SMD]"]
  R2 = Resistor [tolerance=±5% resistance=1.8k package="2010 [SMD]"]
  HC-06_Bluetooth = Bluetooth HC-06d [package=THT]
  Pro_Micro1 = SparkFun Pro Micro  # not connected
  Pro_Micro2 = Pro Micro
  IC1 = L293D [package=THT]
  Lego_Motor = DC Motor
  Battery_for_Lego_motor = Battery block 9V
  Battery_for_Arduino = Battery block 9V

nets:
  N1: R1.Pin_0, R2.Pin_1, HC-06_Bluetooth.RXD
  N2: R1.Pin_1, HC-06_Bluetooth.GND, Pro_Micro2.GND#4, IC1.0V, Battery_for_Lego_motor.-, Battery_for_Arduino.-
  N3: R2.Pin_0, Pro_Micro2.D15/SCLK
  VCC: HC-06_Bluetooth.VCC, Pro_Micro2.VCC
  N4: HC-06_Bluetooth.TXD, Pro_Micro2.D8
  N5: Pro_Micro2.D6, IC1.+V
  N6: Pro_Micro2.D9, IC1.In_4
  N7: Pro_Micro2.RAW, Battery_for_Arduino.+
  N8: IC1.Enable_2, Battery_for_Lego_motor.+
  N9: IC1.Out_3_(_Controlled_by_Enable_2_), Lego_Motor.pin_2
  N10: IC1.Out_4_(_Controlled_by_Enable_2_), Lego_Motor.pin_1

custom parts:
  Bluetooth HC-06d: Bluetooth HC-06 - face down, pins down 16.5mm x 37.5mm PCB
  SparkFun Pro Micro: The Pro Micro is similar to the Pro Mini except with an ATmega32U4 on board. The USB transceiver inside the 32U4 allows us to add USB connectivity on-board and do away with bulky external USB interface. Based on: https://github.com/unorthodox-engineers/unorthodox-arduino/blob/master/Unorthodox/fritzing/parts/Pro%20Micro.fzpz
  Pro Micro: The SparkFun Pro Micro is a complete USB-based microcontoller development system, in a very small footprint, capable of implementing many types of projects. All programming can be done via the USB port.
